# Fritzing sketch Heijunka_ESP_Max7219 (saved by Fritzing 0.9.3b)

parts:
  ZS-042_RTC2 = ZS-042 RTC Module
  M1 = MAX7219 8x8 single Led Matrix Module
  M2 = MAX7219 8x8 single Led Matrix Module  # not connected
  M3 = MAX7219 8x8 single Led Matrix Module  # not connected
  M4 = MAX7219 8x8 single Led Matrix Module  # not connected
  Mod1 = Amica NodeMCU DevKit 1.0
  U2 = 2RelayModule
  S2 = Square Pushbutton

nets:
  GND: ZS-042_RTC2.GND, M1.I-GND, M1.O-GND, Mod1.pin2, Mod1.pin_25, U2.GND, S2.leg0
  VCC: ZS-042_RTC2.VCC, M1.I-VCC, M1.O-VCC, Mod1.pin1, Mod1.pin_26, U2.VCC
  N1: ZS-042_RTC2.SDA, Mod1.pin_13
  N2: ZS-042_RTC2.SCL, Mod1.pin_14
  N3: M1.I-CLK, M1.O-CLK, Mod1.pin8
  N4: M1.I-CS, M1.O-CS, Mod1.pin5
  N5: M1.I-DIN, Mod1.pin6
  N6: Mod1.pin_11, U2.IN1
  N7: Mod1.pin_12, S2.leg1

custom parts:
  MAX7219 8x8 single Led Matrix Module: Description: MAX7219 8x8 LedMatrix single Red Module Dimensions: 32x32mm Documents:
  Amica NodeMCU DevKit 1.0: Amica NodeMCU DevKit 1.0 Development Kit based on ESP8266 ESP-12E, integating GPIO, PWM, IIC, 1-Wire and ADC all in one board. Links: NodeMCU information page Github
  2RelayModule: 2 relay arduino module SONGLE SRD05VDC-SL-C
